# Fritzing sketch DoserPCB (saved by Fritzing 1.0.5)
circuit board: 8.46667cm x 5.64444cm
breadboards: 1

parts:
  Nano4 = Arduino Nano v2.3
  C16 = Electrolytic Capacitor [capacitance=1000µF package="300 mil [THT, electrolytic]"]
  R15 = Resistor [tolerance=±5% resistance=220 power=0.25W package=THT]
  R17 = Resistor [tolerance=±5% resistance=220 power=0.25W package=THT]
  Q12 = MOSFET-NCHANNEL [package=to220v]
  Q11 = MOSFET-NCHANNEL [package=to220v]
  Q13 = MOSFET-NCHANNEL [package=to220v]
  R16 = Resistor [tolerance=±5% resistance=220 power=0.25W package=THT]
  J1 = Screw terminal - 2 pins [package=THT]
  J2 = Screw terminal - 2 pins [package=THT]
  J3 = Screw terminal - 2 pins [package=THT]
  J4 = Screw terminal - 2 pins [package=THT]
  R18 = Resistor [tolerance=±5% resistance=10k power=0.25W package=THT]
  R19 = Resistor [tolerance=±5% resistance=10k power=0.25W package=THT]
  R20 = Resistor [tolerance=±5% resistance=10k power=0.25W package=THT]
  D1 = Rectifier Diode [part_number=1N4001 package="300 mil [THT]"]
  D2 = Rectifier Diode [part_number=1N4001 package="300 mil [THT]"]
  D3 = Rectifier Diode [part_number=1N4001 package="300 mil [THT]"]

nets:
  N1: Nano4.RST, R18.Pin_0
  N2: Nano4.GND, C16.-, R17.Pin_1, Q11.G, J4.pin2, R19.Pin_0, R20.Pin_0
  N3: Nano4.D2, R15.Pin_0
  N4: Nano4.D3, R16.Pin_0
  N5: Nano4.D4, R17.Pin_0
  N6: Nano4.VIN, C16.+, J1.pin1, J2.pin1, J3.pin1, J4.pin1, D1.cathode, D2.cathode, D3.cathode
  N7: R15.Pin_1, Q13.G
  N8: Q12.G, R16.Pin_1
  N9: Q12.D, J2.pin2, D2.anode
  N10: Q12.S, R19.Pin_1
  N11: Q11.D, J1.pin2, D1.anode
  N12: Q11.S, R20.Pin_1
  N13: Q13.D, J3.pin2, D3.anode
  N14: Q13.S, R18.Pin_1
